// Logisim project 4 Bit Adder Subtractor.circ as structural Verilog: 3 circuits, main circuit main
module main (
  input  Cin,
  input  A0,
  input  A1,
  input  A2,
  input  A3,
  input  B0,
  input  B1,
  input  B2,
  input  B3,
  output S0,
  output S1,
  output S2,
  output S3,
  output Cout
);

  _4_bit_Adder_Subtractor u_4_bit_adder_subtractor_1 (
    .Cout(S0), .Cin(Cin), .A0(A0), .A1(A1), .A2(A2), .A3(A3), .B0(B0), .B1(B1), .S0(S1), .B2(B2), .S1(S2),
    .S2(S3), .S3(Cout), .B3(B3));
endmodule

module Full_Adder (
  input  Cin,
  input  A,
  input  B,
  output S0,
  output Cout
);

  wire and_1_out, and_2_out, xor_1_out;

  xor xor_1 (xor_1_out, Cin, A);
  and and_1 (and_1_out, Cin, A);
  xor xor_2 (S0, xor_1_out, B);
  and and_2 (and_2_out, xor_1_out, B);
  or or_1 (Cout, and_1_out, and_2_out);
endmodule

module _4_bit_Adder_Subtractor (
  input  Cin,
  input  A0,
  input  A1,
  input  A2,
  input  A3,
  input  B0,
  input  B1,
  input  B2,
  input  B3,
  output S0,
  output S1,
  output S2,
  output S3,
  output Cout
);

  wire full_adder_1_s0, full_adder_2_s0, full_adder_3_s0, xor_1_out, xor_2_out, xor_3_out, xor_4_out;

  xor xor_1 (xor_1_out, Cin, B0);
  xor xor_2 (xor_2_out, Cin, B1);
  xor xor_3 (xor_3_out, Cin, B2);
  xor xor_4 (xor_4_out, Cin, B3);
  Full_Adder full_adder_1 (.Cin(Cin), .A(A0), .B(xor_1_out), .S0(full_adder_1_s0), .Cout(S0));
  Full_Adder full_adder_2 (.Cin(full_adder_1_s0), .A(A1), .B(xor_2_out), .S0(full_adder_2_s0), .Cout(S1));
  Full_Adder full_adder_3 (.Cin(full_adder_2_s0), .A(A2), .B(xor_3_out), .S0(full_adder_3_s0), .Cout(S2));
  Full_Adder full_adder_4 (.Cin(full_adder_3_s0), .A(A3), .B(xor_4_out), .S0(Cout), .Cout(S3));
endmodule
